# Fritzing sketch Circuit_diagram (saved by Fritzing 0.9.2b)

parts:
  U1 = LCD-16X2 [package=lcd-16x2]
  Part1 = Arduino Uno (Rev3) - ICSP
  BAT1 = Battery Holders [package=lipo-1100mAh]

nets:
  VSS: U1.VSS, Part1.GND
  VDD: U1.VDD, Part1.5V
  N1: U1.VO, Part1.D6_PWM
  N2: U1.RS, Part1.ICSP_MISO, Part1.D12/MISO
  N3: U1.E, Part1.ICSP_MOSI, Part1.D11_PWM/MOSI
  N4: U1.DB4, Part1.D5_PWM
  N5: U1.DB5, Part1.D4
  N6: U1.DB6, Part1.D3_PWM
  N7: U1.DB7, Part1.D2
  N8: Part1.A1, BAT1.+
